// Logisim project Unicycle Processor.circ as structural Verilog: 1 circuit, main circuit main
module main (
  input  [1:0] in_1,
  input  ENWR,
  input  R,
  input  W,
  input  ClK,
  input  CLK_2,
  input  in_7,
  input  in_8,
  input  [1:0] in_9,
  input  in_10,
  input  [1:0] ALU_OP,
  input  [1:0] in_12
);

  wire alu_controller_1_jr, alu_thirty_two_bits_1_zero, and_1_out;
  wire [2:0] alu_controller_1_alu_op_2;
  wire [4:0] multiplexer_2_out;
  wire [27:0] shifter_1_out;
  wire [31:0] adder_1_out, adder_2_out, adder_3_out, ALURESULT, bit_extender_1_out, DMDATA,
       instruction_memory_1_instruction, multiplexer_3_out, multiplexer_4_out, multiplexer_5_out,
       multiplexer_6_out, multiplexer_8_out, PC_q, PCRESULT, register_bank_1_r1_2, register_bank_1_r2_2,
       shifter_2_out;

  // Control_Unit control_unit_1: pin names not known
  Register #(.width(32)) PC (.D(PCRESULT), .Q(PC_q));  // open: en, clk, clr
  Adder #(.width(32)) adder_1 (.a(32'h4), .b(PC_q), .out(adder_1_out));  // open: cin, cout
  Instruction_Memory instruction_memory_1 (.PC_DIR(PC_q), .INSTRUCTION(instruction_memory_1_instruction));
  Adder #(.width(32)) adder_2 (.a(PC_q), .b(32'h8), .out(adder_2_out));  // open: cin, cout
  Shifter #(.width(28)) shifter_1 (.in(instruction_memory_1_instruction[27:0]), .\dist (5'b00010), .out(shifter_1_out));
  Multiplexer #(.select(2), .width(32)) multiplexer_1 (
    .in0(ALURESULT), .in1(DMDATA), .in2(adder_2_out), .in3({32{1'b0}}), .sel(in_12));  // open: out, en
  Multiplexer #(.select(2), .width(5)) multiplexer_2 (
    .in0(instruction_memory_1_instruction[20:16]), .in1(instruction_memory_1_instruction[15:11]),
    .in2({5{1'b1}}), .in3({5{1'b0}}), .out(multiplexer_2_out), .sel(in_9));  // open: en
  Register_Bank register_bank_1 (
    .Clk(ClK), .R1(instruction_memory_1_instruction[25:21]), .R2(instruction_memory_1_instruction[20:16]),
    .WR(multiplexer_2_out), .WD(multiplexer_3_out), .ENWR(ENWR), .R1_2(register_bank_1_r1_2),
    .R2_2(register_bank_1_r2_2));
  Multiplexer #(.width(32)) multiplexer_3 (
    .in0(multiplexer_8_out), .in1(adder_2_out), .out(multiplexer_3_out), .sel(in_10));  // open: en
  assign bit_extender_1_out = {{16{instruction_memory_1_instruction[15]}}, instruction_memory_1_instruction[15:0]};  // Bit_Extender bit_extender_1
  Multiplexer #(.width(32)) multiplexer_4 (
    .in0(register_bank_1_r2_2), .in1(bit_extender_1_out), .out(multiplexer_4_out), .sel(in_8));  // open: en
  Adder #(.width(32)) adder_3 (.a(adder_1_out), .b(shifter_2_out), .out(adder_3_out));  // open: cin, cout
  Shifter #(.width(32)) shifter_2 (.in(bit_extender_1_out), .\dist (5'b00010), .out(shifter_2_out));
  ALU_Thirty_Two_Bits alu_thirty_two_bits_1 (
    .RESULT(ALURESULT), .ALU_CODE(alu_controller_1_alu_op_2), .R2(multiplexer_4_out), .CIN(1'b0),
    .R1(register_bank_1_r1_2), .ZERO(alu_thirty_two_bits_1_zero));
  ALU_Controller alu_controller_1 (
    .FUNCT(instruction_memory_1_instruction[5:0]), .ALU_Op(ALU_OP), .ALU_OP_2(alu_controller_1_alu_op_2),
    .JR(alu_controller_1_jr));
  Multiplexer #(.width(32)) multiplexer_5 (
    .in0(adder_1_out), .in1(adder_3_out), .out(multiplexer_5_out), .sel(and_1_out));  // open: en
  buf and_1 (and_1_out, alu_thirty_two_bits_1_zero);  // AND_Gate
  Multiplexer #(.width(32)) multiplexer_6 (
    .in0(adder_1_out), .in1(register_bank_1_r1_2), .out(multiplexer_6_out), .sel(alu_controller_1_jr));  // open: en
  // Data_Memory data_memory_1: pin names not known; wires that end beside it: ALURESULT, CLK_2, register_bank_1_r2_2, W, R, DMDATA
  Multiplexer #(.select(2), .width(32)) multiplexer_7 (
    .in0({adder_1_out[31:28], shifter_1_out}), .in1({adder_1_out[31:28], shifter_1_out}),
    .in2(multiplexer_6_out), .in3(multiplexer_5_out), .out(PCRESULT), .sel(in_1));  // open: en
  Multiplexer #(.width(32)) multiplexer_8 (
    .in0(ALURESULT), .in1(DMDATA), .out(multiplexer_8_out), .sel(in_7));  // open: en

  // Notes on the sheet:
  //   WD OPTIONS
  //   RD OPTIONS
  //   ADDR OR NORMAL 
  //   NEXT OR JR
  //   TAKE BRANCH
  //   JUMP OPTIONS
endmodule
